# Fritzing sketch SchemaTP3 (saved by Fritzing 0.9.3b)
breadboards: 1

parts:
  ESP32 = Intel Galileo
  BME280 = BME280 Breakout
  Informe_Changement = LED - 3mm [color="Blue (430nm)" package="3 mm [THT]"]
  Etat_Ouvert = LED - 3mm [color="Green (555nm)" package="3 mm [THT]"]
  Etat_Fermer = LED - 3mm [color="Red (633nm)" package="3 mm [THT]"]
  R1 = Resistor [tolerance=±5% resistance=220 package=THT]
  R2 = Resistor [tolerance=±5% resistance=220 package=THT]
  R3 = Resistor [tolerance=±5% resistance=220 package=THT]
  Bouton_Fermeture_Manuel = Pushbutton [package="[THT]"]
  Bouton_Reinitialisation = Pushbutton [package="[THT]"]
  R4 = Resistor [tolerance=±5% resistance=1k package=THT]
  R5 = Resistor [tolerance=±5% resistance=1k package=THT]
  J1 = Infrared Proximity Sensor  # not connected

nets:
  N1: ESP32.A4/SDA, BME280.SDI/SDA
  N2: ESP32.A5/SCL, BME280.SCK/SCL
  N3: ESP32.D9_PWM, Bouton_Reinitialisation.Pin_3, Bouton_Reinitialisation.Pin_4, R5.Pin_1
  N4: ESP32.D10_PWM/SS, Bouton_Fermeture_Manuel.Pin_3, Bouton_Fermeture_Manuel.Pin_4, R4.Pin_1
  GND: ESP32.GND, BME280.GND, Informe_Changement.cathode, Etat_Ouvert.cathode, Etat_Fermer.cathode, Bouton_Fermeture_Manuel.Pin_1, Bouton_Fermeture_Manuel.Pin_2, Bouton_Reinitialisation.Pin_1, Bouton_Reinitialisation.Pin_2
  N5: ESP32.D4, R3.Pin_0
  N6: ESP32.D5_PWM, R2.Pin_0
  N7: ESP32.D6_PWM, R1.Pin_0
  3V3: ESP32.3V3, BME280.3.3V
  N8: ESP32.5V, R4.Pin_0, R5.Pin_0
  N9: Informe_Changement.anode, R3.Pin_1
  N10: Etat_Ouvert.anode, R2.Pin_1
  N11: Etat_Fermer.anode, R1.Pin_1
